// Logisim project multi-cycle-cpu.circ as structural Verilog: 8 circuits, main circuit main
module main (
  input  [7:0] Instruction,
  input  RUN,
  input  RESET,
  output DONE
);

  wire CLOCK_out, control_unit_1_ain, control_unit_1_asen, control_unit_1_bin, control_unit_1_bout,
       control_unit_1_clear, control_unit_1_dinout, control_unit_1_irin, control_unit_1_r0_in,
       control_unit_1_r0_out, control_unit_1_r1_in, control_unit_1_r1_out, control_unit_1_r2_in,
       control_unit_1_r2_out, control_unit_1_r3_in, control_unit_1_r3_out, control_unit_1_r4_in,
       control_unit_1_r4_out, control_unit_1_r5_in, control_unit_1_r5_out, control_unit_1_r6_in,
       control_unit_1_r6_out, control_unit_1_r7_in, control_unit_1_r7_out, n2_bit_counter_1_t0,
       n2_bit_counter_1_t1;
  wire [2:0] priority_encoder_1_out;
  wire [7:0] a_1_a_out, alu_1_aluout, b_1_b_out, ir_1_instruction_2, multiplexer_1_out, multiplexer_2_out,
       multiplexer_3_out, registers_1_r0_out, registers_1_r1_out, registers_1_r2_out, registers_1_r3_out,
       registers_1_r4_out, registers_1_r5_out, registers_1_r6_out, registers_1_r7_out;

  Hex_Digit_Display hex_digit_display_1 (.value(registers_1_r3_out[7:4]));  // open: dp
  Hex_Digit_Display hex_digit_display_2 (.value(registers_1_r4_out[7:4]));  // open: dp
  Hex_Digit_Display hex_digit_display_3 (.value(registers_1_r3_out[3:0]));  // open: dp
  Hex_Digit_Display hex_digit_display_4 (.value(registers_1_r4_out[3:0]));  // open: dp
  Registers registers_1 (
    .CLOCK(CLOCK_out), .BUS_IN(multiplexer_3_out), .R0_in(control_unit_1_r0_in),
    .R1_in(control_unit_1_r1_in), .R2_in(control_unit_1_r2_in), .R3_in(control_unit_1_r3_in),
    .R4_in(control_unit_1_r4_in), .R5_in(control_unit_1_r5_in), .R6_in(control_unit_1_r6_in),
    .R7_in(control_unit_1_r7_in), .R0_out(registers_1_r0_out), .R1_out(registers_1_r1_out),
    .R2_out(registers_1_r2_out), .R3_out(registers_1_r3_out), .R4_out(registers_1_r4_out),
    .R5_out(registers_1_r5_out), .R6_out(registers_1_r6_out), .R7_out(registers_1_r7_out));
  Ir ir_1 (
    .Instruction(Instruction), .IRin(control_unit_1_irin), .CLOCK(CLOCK_out),
    .Instruction_2(ir_1_instruction_2));
  Multiplexer #(.select(3), .width(8)) multiplexer_1 (
    .in0(registers_1_r0_out), .in1(registers_1_r1_out), .in2(registers_1_r2_out), .in3(registers_1_r3_out),
    .in4(registers_1_r4_out), .in5(registers_1_r5_out), .in6(registers_1_r6_out), .in7(registers_1_r7_out),
    .out(multiplexer_1_out), .sel(priority_encoder_1_out));  // open: en
  Control_Unit control_unit_1 (
    .Instruction(ir_1_instruction_2), .T1(n2_bit_counter_1_t1), .T0(n2_bit_counter_1_t0), .RESET(RESET),
    .R0_in(control_unit_1_r0_in), .R1_in(control_unit_1_r1_in), .R2_in(control_unit_1_r2_in),
    .R3_in(control_unit_1_r3_in), .R4_in(control_unit_1_r4_in), .R5_in(control_unit_1_r5_in),
    .R6_in(control_unit_1_r6_in), .R7_in(control_unit_1_r7_in), .R0_out(control_unit_1_r0_out),
    .R1_out(control_unit_1_r1_out), .R2_out(control_unit_1_r2_out), .R3_out(control_unit_1_r3_out),
    .R4_out(control_unit_1_r4_out), .R5_out(control_unit_1_r5_out), .R6_out(control_unit_1_r6_out),
    .R7_out(control_unit_1_r7_out), .IRin(control_unit_1_irin), .Ain(control_unit_1_ain),
    .Bin(control_unit_1_bin), .Bout(control_unit_1_bout), .Done(DONE), .CLEAR(control_unit_1_clear),
    .Asen(control_unit_1_asen), .DINout(control_unit_1_dinout));  // open: Rxin, Ryout, Rxout
  _2_Bit_COunter u_2_bit_counter_1 (
    .CLOCK(CLOCK_out), .RUN(RUN), .RESET(control_unit_1_clear), .T1(n2_bit_counter_1_t1),
    .T0(n2_bit_counter_1_t0));
  Multiplexer #(.width(8)) multiplexer_2 (
    .in0(multiplexer_1_out), .in1(Instruction), .out(multiplexer_2_out), .sel(control_unit_1_dinout));  // open: en
  Multiplexer #(.width(8)) multiplexer_3 (
    .in0(multiplexer_2_out), .in1(b_1_b_out), .out(multiplexer_3_out), .sel(control_unit_1_bout));  // open: en
  Priority_Encoder priority_encoder_1 (
    .in0(control_unit_1_r0_out), .in1(control_unit_1_r1_out), .in2(control_unit_1_r2_out),
    .in3(control_unit_1_r3_out), .in4(control_unit_1_r4_out), .in5(control_unit_1_r5_out),
    .in6(control_unit_1_r6_out), .in7(control_unit_1_r7_out), .out(priority_encoder_1_out));  // open: en_in
  A a_1 (.BUS_IN(multiplexer_3_out), .Ain(control_unit_1_ain), .CLOCK(CLOCK_out), .A_out(a_1_a_out));
  Clock CLOCK (.out(CLOCK_out));
  ALU alu_1 (.BUS_IN(multiplexer_3_out), .A_out(a_1_a_out), .Asen(control_unit_1_asen), .ALUout(alu_1_aluout));
  B b_1 (.ALUout(alu_1_aluout), .Bin(control_unit_1_bin), .CLOCK(CLOCK_out), .B_out(b_1_b_out));
endmodule

module Registers (
  input  CLOCK,
  input  [7:0] BUS_IN,
  input  R0_in,
  input  R1_in,
  input  R2_in,
  input  R3_in,
  input  R4_in,
  input  R5_in,
  input  R6_in,
  input  R7_in,
  output [7:0] R0_out,
  output [7:0] R1_out,
  output [7:0] R2_out,
  output [7:0] R3_out,
  output [7:0] R4_out,
  output [7:0] R5_out,
  output [7:0] R6_out,
  output [7:0] R7_out
);

  Register register_1 (.D(BUS_IN), .en(R0_in), .Q(R0_out), .clk(CLOCK));  // open: clr
  Register register_2 (.D(BUS_IN), .en(R1_in), .Q(R1_out), .clk(CLOCK));  // open: clr
  Register register_3 (.D(BUS_IN), .en(R2_in), .Q(R2_out), .clk(CLOCK));  // open: clr
  Register register_4 (.D(BUS_IN), .en(R3_in), .Q(R3_out), .clk(CLOCK));  // open: clr
  Register register_5 (.D(BUS_IN), .en(R4_in), .Q(R4_out), .clk(CLOCK));  // open: clr
  Register register_6 (.D(BUS_IN), .en(R5_in), .Q(R5_out), .clk(CLOCK));  // open: clr
  Register register_7 (.D(BUS_IN), .en(R6_in), .Q(R6_out), .clk(CLOCK));  // open: clr
  Register register_8 (.D(BUS_IN), .en(R7_in), .Q(R7_out), .clk(CLOCK));  // open: clr
endmodule

module Control_Unit (
  input  [7:0] Instruction,
  input  T1,
  input  T0,
  input  RESET,
  output IRin,
  output Rxin,
  output Ain,
  output Bin,
  output Bout,
  output Done,
  output R0_in,
  output R1_in,
  output R2_in,
  output R3_in,
  output R4_in,
  output R5_in,
  output R6_in,
  output R7_in,
  output CLEAR,
  output Ryout,
  output R0_out,
  output R1_out,
  output R2_out,
  output R3_out,
  output R4_out,
  output R5_out,
  output R6_out,
  output R7_out,
  output Asen,
  output DINout,
  output Rxout
);

  wire and_3_out, and_4_out, and_7_out, and_8_out, and_9_out, and_10_out, not_1_out, not_2_out, not_3_out,
       not_4_out, not_5_out, not_6_out, not_7_out, not_8_out, not_9_out, not_10_out, not_11_out, not_12_out,
       not_13_out, not_14_out, not_15_out, not_16_out, or_1_out;
  wire [2:0] multiplexer_1_out;

  Multiplexer #(.width(3)) multiplexer_1 (
    .in0(Instruction[5:3]), .in1(Instruction[2:0]), .out(multiplexer_1_out), .sel(Ryout));  // open: en
  Decoder #(.select(3), .disabled(0)) decoder_1 (
    .out0(R0_in), .out1(R1_in), .out2(R2_in), .out3(R3_in), .out4(R4_in), .out5(R5_in), .out6(R6_in),
    .out7(R7_in), .sel(Instruction[5:3]), .en(Rxin));
  or or_1 (or_1_out, Ryout, Rxout);
  Decoder #(.select(3), .disabled(0)) decoder_2 (
    .out0(R0_out), .out1(R1_out), .out2(R2_out), .out3(R3_out), .out4(R4_out), .out5(R5_out), .out6(R6_out),
    .out7(R7_out), .sel(multiplexer_1_out), .en(or_1_out));
  not not_1 (not_1_out, T0);
  not not_2 (not_2_out, T1);
  not not_3 (not_3_out, Instruction[7]);
  not not_4 (not_4_out, T1);
  not not_5 (not_5_out, T1);
  not not_6 (not_6_out, T0);
  and and_1 (Bout, Instruction[7], T1, T0);
  not not_7 (not_7_out, Instruction[7]);
  not not_8 (not_8_out, T1);
  not not_9 (not_9_out, Instruction[7]);
  not not_10 (not_10_out, Instruction[6]);
  not not_11 (not_11_out, T1);
  not not_12 (not_12_out, T0);
  not not_13 (not_13_out, T0);
  not not_14 (not_14_out, Instruction[7]);
  not not_15 (not_15_out, T1);
  not not_16 (not_16_out, T1);
  and and_2 (IRin, not_1_out, not_2_out);
  and and_3 (and_3_out, not_3_out, not_4_out, T0);
  or or_2 (Rxin, and_3_out, and_4_out);
  and and_4 (and_4_out, Instruction[7], T1, T0);
  and and_5 (Ain, Instruction[7], not_5_out, T0);
  and and_6 (Bin, Instruction[7], T1, not_6_out);
  and and_7 (and_7_out, not_7_out, not_8_out, T0);
  or or_3 (Done, and_7_out, and_8_out);
  and and_8 (and_8_out, Instruction[7], T1, T0);
  and and_9 (and_9_out, not_9_out, not_10_out, not_11_out, T0);
  and and_10 (and_10_out, Instruction[7], T1, not_12_out);
  and and_11 (Asen, Instruction[7], Instruction[6], T1, not_13_out);
  and and_12 (DINout, not_14_out, Instruction[6], not_15_out, T0);
  and and_13 (Rxout, Instruction[7], not_16_out, T0);
  or or_4 (Ryout, and_9_out, and_10_out);
  or or_5 (CLEAR, RESET, Done);

  // Notes on the sheet:
  //   Op2
  //   Op1
endmodule

module B (
  input  [7:0] ALUout,
  input  Bin,
  input  CLOCK,
  output [7:0] B_out
);

  Register register_1 (.D(ALUout), .en(Bin), .Q(B_out), .clk(CLOCK));  // open: clr
endmodule

// IR
module Ir (
  input  [7:0] Instruction,
  input  IRin,
  input  CLOCK,
  output [7:0] Instruction_2
);

  Register register_1 (.D(Instruction), .en(IRin), .Q(Instruction_2), .clk(CLOCK));  // open: clr
endmodule

module A (
  input  [7:0] BUS_IN,
  input  Ain,
  input  CLOCK,
  output [7:0] A_out
);

  Register register_1 (.D(BUS_IN), .en(Ain), .Q(A_out), .clk(CLOCK));  // open: clr
endmodule

module ALU (
  input  [7:0] BUS_IN,
  input  [7:0] A_out,
  input  Asen,
  output [7:0] ALUout
);

  wire [7:0] adder_1_out, subtractor_1_out;

  Adder adder_1 (.a(BUS_IN), .b(A_out), .out(adder_1_out));  // open: cin, cout
  Subtractor subtractor_1 (.a(A_out), .b(BUS_IN), .out(subtractor_1_out));  // open: bin, bout
  Multiplexer #(.width(8)) multiplexer_1 (
    .in0(adder_1_out), .in1(subtractor_1_out), .out(ALUout), .sel(Asen));  // open: en
endmodule

// Counter
module _2_Bit_COunter (
  input  CLOCK,
  input  RUN,
  input  RESET,
  output T1,
  output T0
);

  wire and_1_out, and_2_out, d_ff_2_qn, not_1_out, not_2_out, xor_1_out;

  not not_1 (not_1_out, RESET);
  not not_2 (not_2_out, CLOCK);
  and and_1 (and_1_out, not_1_out, xor_1_out);
  D_Flip_Flop d_ff_1 (.clk(not_2_out), .D(and_1_out), .Q(T1), .en(RUN));  // open: Qn, preset, reset
  and and_2 (and_2_out, not_1_out, d_ff_2_qn);
  D_Flip_Flop d_ff_2 (.clk(not_2_out), .D(and_2_out), .Q(T0), .Qn(d_ff_2_qn), .en(RUN));  // open: preset, reset
  xor xor_1 (xor_1_out, T1, T0);
endmodule
